# Fritzing sketch meadow-distance-lcd (saved by Fritzing 0.9.6b)
breadboards: 1

parts:
  Mod1 = Meadow F7 Micro
  Part1 = GY-VL53L0XV2 Laser Ranger Module
  Part2 = ST7789 1.3in 240x240 IPS TFT [part_number=ST7789]

nets:
  VCC: Mod1.3.3V, Part1.VCC, Part1.XSHUT, Part2.VCC
  GND: Mod1.GND, Part1.GND, Part2.GND
  N1: Mod1.SCK, Part2.SCL
  N2: Mod1.MOSI, Part2.SDA
  N3: Mod1.DO0, Part2.RES
  N4: Mod1.DO1, Part2.DC
  N5: Mod1.DO7, Part1.SDA
  N6: Mod1.DO8, Part1.SCL

custom parts:
  GY-VL53L0XV2 Laser Ranger Module: The GY-VL53L0XV2 is based on the VL53L0X from ST Microelectronics, a time-of-flight ranging system integrated into a compact module.
