# Fritzing sketch meadow-distance-sensor (saved by Fritzing 0.9.6b)
breadboards: 1

parts:
  Mod1 = Meadow F7 Micro
  Part1 = GY-VL53L0XV2 Laser Ranger Module

nets:
  3.3V: Mod1.3.3V, Part1.VCC, Part1.XSHUT
  GND: Mod1.GND, Part1.GND
  N1: Mod1.DO7, Part1.SDA
  N2: Mod1.DO8, Part1.SCL

custom parts:
  GY-VL53L0XV2 Laser Ranger Module: The GY-VL53L0XV2 is based on the VL53L0X from ST Microelectronics, a time-of-flight ranging system integrated into a compact module.
